// Logisim project adder.circ as structural Verilog: 14 circuits, main circuit main
module main (
  input  in_1,
  input  in_2,
  input  in_3,
  input  in_4,
  input  in_5,
  input  in_6,
  input  EN,
  input  in_8,
  input  D_E,
  input  [3:0] in_10,
  input  [3:0] in_11,
  output out_12,
  output out_13,
  output out_14,
  output out_15
);

  wire adder_4_1_c4, and_1_out, and_2_out, comparer_4_1_y, decoder_4to16_1_y0, decoder_4to16_1_y1,
       decoder_4to16_1_y2, decoder_4to16_1_y3, decoder_4to16_1_y4, decoder_4to16_1_y5, decoder_4to16_1_y6,
       decoder_4to16_1_y7, decoder_4to16_1_y8, decoder_4to16_1_y9, decoder_4to16_1_y10, decoder_4to16_1_y11,
       decoder_4to16_1_y12, decoder_4to16_1_y13, decoder_4to16_1_y14, decoder_4to16_1_y15, dipswitch_1_p1,
       dipswitch_1_p2, dipswitch_2_p1, dipswitch_2_p2, dipswitch_2_p3, dipswitch_2_p4, dipswitch_2_p5,
       dipswitch_2_p6, half_adder_1_1_c, half_adder_1_1_s, half_adder_1_2_c, not_1_out, not_2_out, not_3_out,
       or_1_out, or_2_out, or_3_out, or_4_out, or_6_out, or_7_out, or_8_out, or_9_out, undriven;
  wire [3:0] adder_4_1_s0;

  // DipSwitch #(.number(4)) dipswitch_1: pin names not known; wires that end beside it: dipswitch_1_p1, dipswitch_1_p2
  // DipSwitch #(.number(4)) dipswitch_2: pin names not known; wires that end beside it: dipswitch_2_p1, dipswitch_2_p2, dipswitch_2_p3, dipswitch_2_p4, dipswitch_2_p5, dipswitch_2_p6
  and and_1 (and_1_out, in_11[3], not_1_out, in_10[3]);
  not not_1 (not_1_out, adder_4_1_s0[3]);
  LED led_1 (.in(comparer_4_1_y));
  comparer_4 comparer_4_1 (
    .A0(dipswitch_1_p1), .A1(dipswitch_1_p2), .A2(dipswitch_2_p1), .A3(dipswitch_2_p2), .B0(dipswitch_2_p3),
    .B1(dipswitch_2_p4), .B2(dipswitch_2_p5), .B3(dipswitch_2_p6), .EN(EN), .Y(comparer_4_1_y));
  not not_2 (not_2_out, in_11[3]);
  not not_3 (not_3_out, in_10[3]);
  or or_1 (or_1_out, and_1_out, and_2_out);
  adder_4 adder_4_1 (
    .C0(in_8), .B3(in_11[3]), .B2(in_11[2]), .B1(in_11[1]), .B0(in_11[0]), .A3(in_10[3]), .A2(in_10[2]),
    .A1(in_10[1]), .A0(in_10[0]), .S3(adder_4_1_s0[3]), .S2(adder_4_1_s0[2]), .S1(adder_4_1_s0[1]),
    .S0(adder_4_1_s0[0]), .C4(adder_4_1_c4));
  subtractor_4 subtractor_4_1 ();  // open: Bin, B3, B2, B1, B0, A3, A2, A1, A0, S3, S2, S1, S0, Bout
  LED led_2 (.in(adder_4_1_c4));
  and and_2 (and_2_out, not_3_out, adder_4_1_s0[3], not_2_out);
  full_adder_1 full_adder_1_1 (.A(in_1), .B(in_3), .Cin(in_5), .S(out_12), .Cout(out_13));
  decoder_4to16 decoder_4to16_1 (
    .A0(adder_4_1_s0[0]), .A1(adder_4_1_s0[1]), .A2(adder_4_1_s0[2]), .A3(adder_4_1_s0[3]), .EN(D_E),
    .Y0(decoder_4to16_1_y0), .Y1(decoder_4to16_1_y1), .Y2(decoder_4to16_1_y2), .Y3(decoder_4to16_1_y3),
    .Y4(decoder_4to16_1_y4), .Y5(decoder_4to16_1_y5), .Y6(decoder_4to16_1_y6), .Y7(decoder_4to16_1_y7),
    .Y8(decoder_4to16_1_y8), .Y9(decoder_4to16_1_y9), .Y10(decoder_4to16_1_y10), .Y11(decoder_4to16_1_y11),
    .Y12(decoder_4to16_1_y12), .Y13(decoder_4to16_1_y13), .Y14(decoder_4to16_1_y14), .Y15(decoder_4to16_1_y15));
  or or_2 (or_2_out, decoder_4to16_1_y2, decoder_4to16_1_y3, decoder_4to16_1_y4, decoder_4to16_1_y5, decoder_4to16_1_y6, decoder_4to16_1_y8, decoder_4to16_1_y10, decoder_4to16_1_y11, decoder_4to16_1_y9, decoder_4to16_1_y13, decoder_4to16_1_y14, decoder_4to16_1_y15);
  LED overflow (.in(or_1_out));
  half_adder_1 half_adder_1_1 (.A(in_2), .B(in_4), .C(half_adder_1_1_c), .S(half_adder_1_1_s));
  or or_3 (or_3_out, decoder_4to16_1_y0, decoder_4to16_1_y1, decoder_4to16_1_y4, decoder_4to16_1_y5, decoder_4to16_1_y6, decoder_4to16_1_y8, decoder_4to16_1_y10, decoder_4to16_1_y11, decoder_4to16_1_y12, decoder_4to16_1_y9, decoder_4to16_1_y14, decoder_4to16_1_y15);
  _7_Segment_Display u_7_segment_display_1 (.g(adder_4_1_s0[3]));  // open: f, a, b, e, d, c, dp
  _7_Segment_Display u_7_segment_display_2 (
    .g(or_2_out), .f(or_3_out), .a(or_4_out), .b(or_6_out), .e(or_7_out), .d(or_8_out), .c(or_9_out),
    .dp(undriven));
  half_adder_1 half_adder_1_2 (.A(half_adder_1_1_s), .B(in_6), .C(half_adder_1_2_c), .S(out_15));
  or or_4 (or_4_out, decoder_4to16_1_y0, decoder_4to16_1_y2, decoder_4to16_1_y3, decoder_4to16_1_y5, decoder_4to16_1_y6, decoder_4to16_1_y7, decoder_4to16_1_y9, decoder_4to16_1_y10, decoder_4to16_1_y12, decoder_4to16_1_y8, decoder_4to16_1_y14, decoder_4to16_1_y15);
  or or_5 (out_14, half_adder_1_1_c, half_adder_1_2_c);
  or or_6 (or_6_out, decoder_4to16_1_y3, decoder_4to16_1_y4, decoder_4to16_1_y7, decoder_4to16_1_y8, decoder_4to16_1_y2, decoder_4to16_1_y9, decoder_4to16_1_y10, decoder_4to16_1_y0, decoder_4to16_1_y13);
  or or_7 (or_7_out, decoder_4to16_1_y1, decoder_4to16_1_y2, decoder_4to16_1_y10, decoder_4to16_1_y6, decoder_4to16_1_y8, decoder_4to16_1_y11, decoder_4to16_1_y12, decoder_4to16_1_y13, decoder_4to16_1_y14, decoder_4to16_1_y15, decoder_4to16_1_y0);
  or or_8 (or_8_out, decoder_4to16_1_y2, decoder_4to16_1_y3, decoder_4to16_1_y5, decoder_4to16_1_y6, decoder_4to16_1_y8, decoder_4to16_1_y9, decoder_4to16_1_y11, decoder_4to16_1_y12, decoder_4to16_1_y13, decoder_4to16_1_y14, decoder_4to16_1_y0);
  or or_9 (or_9_out, decoder_4to16_1_y3, decoder_4to16_1_y4, decoder_4to16_1_y5, decoder_4to16_1_y6, decoder_4to16_1_y7, decoder_4to16_1_y0, decoder_4to16_1_y9, decoder_4to16_1_y10, decoder_4to16_1_y11, decoder_4to16_1_y8, decoder_4to16_1_y13);

  // Notes on the sheet:
  //   Implement 4-bit unsigned adder with overflow detection, and also be able to determine positive/negative using 
  //   the sign bit. However, this function must be implemented with two's complement. (Converting the output to sign-magnitude representation before connecting to seg7.)
endmodule

module mux_2to1 (
  input  D0,
  input  D1,
  input  S,
  input  EN,
  output Y
);

  wire and_1_out, and_2_out, decoder_1to2_1_y0, decoder_1to2_1_y1;

  decoder_1to2 decoder_1to2_1 (.A0(S), .EN(EN), .Y0(decoder_1to2_1_y0), .Y1(decoder_1to2_1_y1));
  and and_1 (and_1_out, D0, decoder_1to2_1_y0);
  and and_2 (and_2_out, decoder_1to2_1_y1, D1);
  or or_1 (Y, and_1_out, and_2_out);
endmodule

module decoder_1to2 (
  input  A0,
  input  EN,
  output Y0,
  output Y1
);

  wire not_1_out;

  not not_1 (not_1_out, A0);
  and and_1 (Y0, not_1_out, EN);
  and and_2 (Y1, A0, EN);
endmodule

module mux_4to1 (
  input  D0,
  input  D1,
  input  D2,
  input  D3,
  input  S1,
  input  S0,
  input  EN,
  output Y
);

  wire mux_2to1_1_y, mux_2to1_2_y;

  mux_2to1 mux_2to1_1 (.D0(D0), .D1(D1), .S(S0), .EN(EN), .Y(mux_2to1_1_y));
  mux_2to1 mux_2to1_2 (.D0(D2), .D1(D3), .S(S0), .EN(EN), .Y(mux_2to1_2_y));
  mux_2to1 mux_2to1_3 (.D0(mux_2to1_1_y), .D1(mux_2to1_2_y), .S(S1), .EN(EN), .Y(Y));
endmodule

module decoder_2to4 (
  input  A0,
  input  A1,
  input  EN,
  output Y0,
  output Y1,
  output Y2,
  output Y3
);

  wire not_1_out, not_2_out;

  not not_1 (not_1_out, A0);
  not not_2 (not_2_out, A1);
  and and_1 (Y0, not_1_out, EN, not_2_out);
  and and_2 (Y1, A0, EN, not_2_out);
  and and_3 (Y2, not_1_out, EN, A1);
  and and_4 (Y3, A0, EN, A1);
endmodule

module comparer_4 (
  input  A0,
  input  A1,
  input  A2,
  input  A3,
  input  B0,
  input  B1,
  input  B2,
  input  B3,
  input  EN,
  output Y
);

  wire xnor_1_out, xnor_2_out, xnor_3_out, xnor_4_out;

  xnor xnor_1 (xnor_1_out, A0, B0);
  xnor xnor_2 (xnor_2_out, A1, B1);
  xnor xnor_3 (xnor_3_out, A2, B2);
  xnor xnor_4 (xnor_4_out, A3, B3);
  and and_1 (Y, xnor_1_out, xnor_2_out, EN, xnor_3_out, xnor_4_out);
endmodule

module half_adder_1 (
  input  A,
  input  B,
  output C,
  output S
);

  and and_1 (C, A, B);
  xor xor_1 (S, A, B);
endmodule

module full_adder_1 (
  input  A,
  input  B,
  input  Cin,
  output S,
  output Cout
);

  wire and_1_out, and_2_out, or_1_out, xor_1_out;

  xor xor_1 (xor_1_out, A, B);
  and and_1 (and_1_out, A, B);
  or or_1 (or_1_out, A, B);
  and and_2 (and_2_out, or_1_out, Cin);
  xor xor_2 (S, xor_1_out, Cin);
  or or_2 (Cout, and_1_out, and_2_out);
endmodule

module adder_4 (
  input  C0,
  input  B3,
  input  B2,
  input  B1,
  input  B0,
  input  A3,
  input  A2,
  input  A1,
  input  A0,
  output S3,
  output S2,
  output S1,
  output S0,
  output C4
);

  wire full_adder_1_2_cout, full_adder_1_3_cout, full_adder_1_4_cout;

  full_adder_1 full_adder_1_1 (.A(A3), .B(B3), .Cin(full_adder_1_2_cout), .S(S3), .Cout(C4));
  full_adder_1 full_adder_1_2 (.A(A2), .B(B2), .Cin(full_adder_1_3_cout), .S(S2), .Cout(full_adder_1_2_cout));
  full_adder_1 full_adder_1_3 (.A(A1), .B(B1), .Cin(full_adder_1_4_cout), .S(S1), .Cout(full_adder_1_3_cout));
  full_adder_1 full_adder_1_4 (.A(A0), .B(B0), .Cin(C0), .S(S0), .Cout(full_adder_1_4_cout));
endmodule

module decoder_4to16 (
  input  A0,
  input  A1,
  input  A2,
  input  A3,
  input  EN,
  output Y0,
  output Y1,
  output Y2,
  output Y3,
  output Y4,
  output Y5,
  output Y6,
  output Y7,
  output Y8,
  output Y9,
  output Y10,
  output Y11,
  output Y12,
  output Y13,
  output Y14,
  output Y15
);

  wire and_1_out, and_2_out, not_1_out;

  not not_1 (not_1_out, A3);
  and and_1 (and_1_out, not_1_out, EN);
  and and_2 (and_2_out, EN, A3);
  decoder_3to8 decoder_3to8_1 (
    .A0(A0), .A1(A1), .A2(A2), .EN(and_1_out), .out_5(Y0), .out_6(Y1), .out_7(Y2), .out_8(Y3), .out_9(Y4),
    .out_10(Y5), .out_11(Y6), .out_12(Y7));
  decoder_3to8 decoder_3to8_2 (
    .A0(A0), .A1(A1), .A2(A2), .EN(and_2_out), .out_5(Y8), .out_6(Y9), .out_7(Y10), .out_8(Y11), .out_9(Y12),
    .out_10(Y13), .out_11(Y14), .out_12(Y15));
endmodule

module decoder_3to8 (
  input  A0,
  input  A1,
  input  A2,
  input  EN,
  output out_5,
  output out_6,
  output out_7,
  output out_8,
  output out_9,
  output out_10,
  output out_11,
  output out_12
);

  wire and_1_out, and_2_out, not_1_out;

  not not_1 (not_1_out, A2);
  and and_1 (and_1_out, not_1_out, EN);
  and and_2 (and_2_out, EN, A2);
  // Probe on out_5
  decoder_2to4 decoder_2to4_1 (.A0(A0), .A1(A1), .EN(and_1_out), .Y0(out_5), .Y1(out_6), .Y2(out_7), .Y3(out_8));
  decoder_2to4 decoder_2to4_2 (.A0(A0), .A1(A1), .EN(and_2_out), .Y0(out_9), .Y1(out_10), .Y2(out_11), .Y3(out_12));
endmodule

module subtractor_4 (
  input  Bin,
  input  B3,
  input  B2,
  input  B1,
  input  B0,
  input  A3,
  input  A2,
  input  A1,
  input  A0,
  output S3,
  output S2,
  output S1,
  output S0,
  output Bout
);

  wire full_subtractor_1_2_bout, full_subtractor_1_3_bout, full_subtractor_1_4_bout;

  full_subtractor_1 full_subtractor_1_1 (.A(A3), .B(B3), .Bin(full_subtractor_1_2_bout), .D(S3), .Bout(Bout));
  full_subtractor_1 full_subtractor_1_2 (
    .A(A2), .B(B2), .Bin(full_subtractor_1_3_bout), .D(S2), .Bout(full_subtractor_1_2_bout));
  full_subtractor_1 full_subtractor_1_3 (
    .A(A1), .B(B1), .Bin(full_subtractor_1_4_bout), .D(S1), .Bout(full_subtractor_1_3_bout));
  full_subtractor_1 full_subtractor_1_4 (.A(A0), .B(B0), .Bin(Bin), .D(S0), .Bout(full_subtractor_1_4_bout));
endmodule

module half_subtractor_1 (
  input  A,
  input  B,
  output Y,
  output C
);

  wire not_1_out;

  not not_1 (not_1_out, A);
  xor xor_1 (Y, A, B);
  and and_1 (C, not_1_out, B);

  // Notes on the sheet:
  //   A-B=Y
endmodule

module full_subtractor_1 (
  input  A,
  input  B,
  input  Bin,
  output D,
  output Bout
);

  wire half_subtractor_1_1_c, half_subtractor_1_1_y, half_subtractor_1_2_c;

  half_subtractor_1 half_subtractor_1_1 (.A(A), .B(B), .Y(half_subtractor_1_1_y), .C(half_subtractor_1_1_c));
  half_subtractor_1 half_subtractor_1_2 (.A(half_subtractor_1_1_y), .B(Bin), .Y(D), .C(half_subtractor_1_2_c));
  or or_1 (Bout, half_subtractor_1_2_c, half_subtractor_1_1_c);
endmodule
