// Logisim project sCPU.circ as structural Verilog: 1 circuit, main circuit main
module main (
  input  addr,
  input  clk,
  output Q2,
  output Q1,
  output Q0
);

  wire and_1_out, and_2_out, and_3_out, and_4_out, and_5_out, and_6_out, b00_q, b01_q, b02_q, b10_q, b11_q,
       b12_q, decoder_1_out0, decoder_1_out1;

  Decoder decoder_1 (.out0(decoder_1_out0), .out1(decoder_1_out1), .sel(addr));  // open: en
  D_Flip_Flop b02 (.clk(clk), .Q(b02_q));  // open: D, Qn, preset, reset
  D_Flip_Flop b12 (.clk(clk), .Q(b12_q));  // open: D, Qn, preset, reset
  and and_1 (and_1_out, decoder_1_out0, b02_q);
  and and_2 (and_2_out, decoder_1_out1, b12_q);
  or or_1 (Q2, and_2_out, and_1_out);
  D_Flip_Flop b01 (.clk(clk), .Q(b01_q));  // open: D, Qn, preset, reset
  D_Flip_Flop b11 (.clk(clk), .Q(b11_q));  // open: D, Qn, preset, reset
  and and_3 (and_3_out, decoder_1_out0, b01_q);
  and and_4 (and_4_out, decoder_1_out1, b11_q);
  D_Flip_Flop b00 (.clk(clk), .Q(b00_q));  // open: D, Qn, preset, reset
  D_Flip_Flop b10 (.clk(clk), .Q(b10_q));  // open: D, Qn, preset, reset
  or or_2 (Q1, and_4_out, and_3_out);
  and and_5 (and_5_out, decoder_1_out0, b00_q);
  and and_6 (and_6_out, decoder_1_out1, b10_q);
  or or_3 (Q0, and_6_out, and_5_out);
endmodule
