// Logisim project seg7.circ as structural Verilog
module main (
  input  D_E,
  input  in_2,
  input  in_3,
  input  in_4,
  input  in_5,
  input  in_6,
  input  in_7,
  input  in_8,
  input  in_9,
  input  in_10,
  input  in_11,
  input  in_12,
  input  in_13,
  input  in_14,
  input  in_15,
  input  in_16,
  input  in_17,
  input  in_18,
  output E_O,
  output E_V
);

  wire decoder_4to16_1_y0, decoder_4to16_1_y1, decoder_4to16_1_y2, decoder_4to16_1_y3, decoder_4to16_1_y4,
       decoder_4to16_1_y5, decoder_4to16_1_y6, decoder_4to16_1_y7, decoder_4to16_1_y8, decoder_4to16_1_y9,
       decoder_4to16_1_y10, decoder_4to16_1_y11, decoder_4to16_1_y12, decoder_4to16_1_y13,
       decoder_4to16_1_y14, decoder_4to16_1_y15, or_1_out, or_2_out, or_3_out, or_4_out, or_5_out, or_6_out,
       or_7_out, undriven;
  wire [3:0] priority_encoder_1_out;

  decoder_4to16 decoder_4to16_1 (
    .A0(priority_encoder_1_out[0]), .A1(priority_encoder_1_out[1]), .A2(priority_encoder_1_out[2]),
    .A3(priority_encoder_1_out[3]), .EN(D_E), .Y0(decoder_4to16_1_y0), .Y1(decoder_4to16_1_y1),
    .Y2(decoder_4to16_1_y2), .Y3(decoder_4to16_1_y3), .Y4(decoder_4to16_1_y4), .Y5(decoder_4to16_1_y5),
    .Y6(decoder_4to16_1_y6), .Y7(decoder_4to16_1_y7), .Y8(decoder_4to16_1_y8), .Y9(decoder_4to16_1_y9),
    .Y10(decoder_4to16_1_y10), .Y11(decoder_4to16_1_y11), .Y12(decoder_4to16_1_y12),
    .Y13(decoder_4to16_1_y13), .Y14(decoder_4to16_1_y14), .Y15(decoder_4to16_1_y15));
  Priority_Encoder #(.select(4)) priority_encoder_1 (
    .in0(in_2), .in1(in_3), .in2(in_4), .in3(in_5), .in4(in_6), .in5(in_7), .in6(in_8), .in7(in_9),
    .in8(in_10), .in9(in_11), .in10(in_12), .in11(in_13), .in12(in_14), .in13(in_15), .in14(in_16),
    .in15(in_17), .out(priority_encoder_1_out), .gs(E_V), .en_out(E_O), .en_in(in_18));
  or or_1 (or_1_out, decoder_4to16_1_y2, decoder_4to16_1_y3, decoder_4to16_1_y4, decoder_4to16_1_y5, decoder_4to16_1_y6, decoder_4to16_1_y8, decoder_4to16_1_y10, decoder_4to16_1_y11, decoder_4to16_1_y9, decoder_4to16_1_y13, decoder_4to16_1_y14, decoder_4to16_1_y15);
  or or_2 (or_2_out, decoder_4to16_1_y0, decoder_4to16_1_y1, decoder_4to16_1_y4, decoder_4to16_1_y5, decoder_4to16_1_y6, decoder_4to16_1_y8, decoder_4to16_1_y10, decoder_4to16_1_y11, decoder_4to16_1_y12, decoder_4to16_1_y9, decoder_4to16_1_y14, decoder_4to16_1_y15);
  _7_Segment_Display u_7_segment_display_1 (
    .g(or_1_out), .f(or_2_out), .a(or_3_out), .b(or_4_out), .e(or_5_out), .d(or_6_out), .c(or_7_out),
    .dp(undriven));
  or or_3 (or_3_out, decoder_4to16_1_y0, decoder_4to16_1_y2, decoder_4to16_1_y3, decoder_4to16_1_y5, decoder_4to16_1_y6, decoder_4to16_1_y7, decoder_4to16_1_y9, decoder_4to16_1_y10, decoder_4to16_1_y12, decoder_4to16_1_y8, decoder_4to16_1_y14, decoder_4to16_1_y15);
  or or_4 (or_4_out, decoder_4to16_1_y3, decoder_4to16_1_y4, decoder_4to16_1_y7, decoder_4to16_1_y8, decoder_4to16_1_y2, decoder_4to16_1_y9, decoder_4to16_1_y10, decoder_4to16_1_y0, decoder_4to16_1_y13);
  or or_5 (or_5_out, decoder_4to16_1_y1, decoder_4to16_1_y2, decoder_4to16_1_y10, decoder_4to16_1_y6, decoder_4to16_1_y8, decoder_4to16_1_y11, decoder_4to16_1_y12, decoder_4to16_1_y13, decoder_4to16_1_y14, decoder_4to16_1_y15, decoder_4to16_1_y0);
  or or_6 (or_6_out, decoder_4to16_1_y2, decoder_4to16_1_y3, decoder_4to16_1_y5, decoder_4to16_1_y6, decoder_4to16_1_y8, decoder_4to16_1_y9, decoder_4to16_1_y11, decoder_4to16_1_y12, decoder_4to16_1_y13, decoder_4to16_1_y14, decoder_4to16_1_y0);
  or or_7 (or_7_out, decoder_4to16_1_y3, decoder_4to16_1_y4, decoder_4to16_1_y5, decoder_4to16_1_y6, decoder_4to16_1_y7, decoder_4to16_1_y0, decoder_4to16_1_y9, decoder_4to16_1_y10, decoder_4to16_1_y11, decoder_4to16_1_y8, decoder_4to16_1_y13);
endmodule

module decoder_4to16 (
  input  A0,
  input  A1,
  input  A2,
  input  A3,
  input  EN,
  output Y0,
  output Y1,
  output Y2,
  output Y3,
  output Y4,
  output Y5,
  output Y6,
  output Y7,
  output Y8,
  output Y9,
  output Y10,
  output Y11,
  output Y12,
  output Y13,
  output Y14,
  output Y15
);

  wire and_1_out, and_2_out, not_1_out;

  not not_1 (not_1_out, A3);
  and and_1 (and_1_out, not_1_out, EN);
  and and_2 (and_2_out, EN, A3);
  decoder_3to8 decoder_3to8_1 (
    .A0(A0), .A1(A1), .A2(A2), .EN(and_1_out), .out_5(Y0), .out_6(Y1), .out_7(Y2), .out_8(Y3), .out_9(Y4),
    .out_10(Y5), .out_11(Y6), .out_12(Y7));
  decoder_3to8 decoder_3to8_2 (
    .A0(A0), .A1(A1), .A2(A2), .EN(and_2_out), .out_5(Y8), .out_6(Y9), .out_7(Y10), .out_8(Y11), .out_9(Y12),
    .out_10(Y13), .out_11(Y14), .out_12(Y15));
endmodule

module decoder_2to4 (
  input  A0,
  input  A1,
  input  EN,
  output Y0,
  output Y1,
  output Y2,
  output Y3
);

  wire not_1_out, not_2_out;

  not not_1 (not_1_out, A0);
  not not_2 (not_2_out, A1);
  and and_1 (Y0, not_1_out, EN, not_2_out);
  and and_2 (Y1, A0, EN, not_2_out);
  and and_3 (Y2, not_1_out, EN, A1);
  and and_4 (Y3, A0, EN, A1);
endmodule

module decoder_3to8 (
  input  A0,
  input  A1,
  input  A2,
  input  EN,
  output out_5,
  output out_6,
  output out_7,
  output out_8,
  output out_9,
  output out_10,
  output out_11,
  output out_12
);

  wire and_1_out, and_2_out, not_1_out;

  not not_1 (not_1_out, A2);
  and and_1 (and_1_out, not_1_out, EN);
  and and_2 (and_2_out, EN, A2);
  // Probe on out_5
  decoder_2to4 decoder_2to4_1 (.A0(A0), .A1(A1), .EN(and_1_out), .Y0(out_5), .Y1(out_6), .Y2(out_7), .Y3(out_8));
  decoder_2to4 decoder_2to4_2 (.A0(A0), .A1(A1), .EN(and_2_out), .Y0(out_9), .Y1(out_10), .Y2(out_11), .Y3(out_12));
endmodule

module encoder_4to2 (
  input  D3,
  input  D2,
  input  D1,
  input  D0,
  output Y0,
  output Y1,
  output V
);

  wire and_1_out, not_1_out;

  not not_1 (not_1_out, D2);
  and and_1 (and_1_out, not_1_out, D1);
  or or_1 (Y1, D2, D3);
  or or_2 (Y0, D3, and_1_out);
  or or_3 (V, Y1, D1, D0);
endmodule

module encoder_8to3 (
  input  in_1,
  input  in_2
);

  encoder_4to2 encoder_4to2_1 ();  // open: D3, D2, D1, D0, Y0, Y1, V
  encoder_4to2 encoder_4to2_2 ();  // open: D3, D2, D1, D0, Y0, Y1, V
endmodule
