// Logisim project xor.circ as structural Verilog: 1 circuit, main circuit main
module main (
  input  in_1,
  input  in_2,
  input  a,
  input  b,
  output out_5,
  output y
);

  wire and_1_out, and_2_out, nand_1_out, nand_2_out, not_1_out, not_2_out, not_3_out, not_4_out;

  not not_1 (not_1_out, in_2);
  not not_2 (not_2_out, in_1);
  not not_3 (not_3_out, b);
  not not_4 (not_4_out, a);
  and and_1 (and_1_out, in_1, not_1_out);
  and and_2 (and_2_out, not_2_out, in_2);
  nand nand_1 (nand_1_out, a, not_3_out);
  nand nand_2 (nand_2_out, not_4_out, b);
  or or_1 (out_5, and_1_out, and_2_out);
  nand nand_3 (y, nand_1_out, nand_2_out);

  // Notes on the sheet:
  //   xor(22)
  //   xor(14)
endmodule
